# Fritzing sketch bbqpi (saved by Fritzing 0.9.3b)
breadboards: 1

parts:
  IC1 = MCP3008 8-channel 10-bit ADC [part_number=MCP3008]
  Raspberry_Pi_1 = Raspberry Pi 3 [part_number=RPI-3-V1.2]
  JP1 = RCA [package=rca_lock]
  JP2 = RCA [package=rca_lock]
  JP3 = RCA [package=rca_lock]
  JP4 = RCA [package=rca_lock]
  Q1 = Basic FET N-Channel [package="TO220 [THT]"]
  J1 = Power Jack [package=power_jack_pth_lock]
  J2 = Power Jack [package=power_jack_pth_lock]
  R1 = Resistor [tolerance=±5% resistance=10k package=THT]
  R2 = Resistor [tolerance=±5% resistance=10k package=THT]
  R3 = Resistor [tolerance=±5% resistance=10k package=THT]
  R4 = Resistor [tolerance=±5% resistance=10k package=THT]
  R5 = Resistor [tolerance=±5% resistance=10k package=THT]
  D1 = Rectifier Diode [part_number=1N4001 package="300 mil [THT]"]

nets:
  N1: IC1.no_name_yet#1, JP1.PIN, R1.Pin_1
  N2: IC1.no_name_yet#2, JP2.PIN, R2.Pin_1
  N3: IC1.no_name_yet#3, JP3.PIN, R3.Pin_1
  N4: IC1.no_name_yet#4, JP4.PIN, R4.Pin_1
  GND: IC1.no_name_yet#9, IC1.no_name_yet#14, Raspberry_Pi_1.GND, Q1.source, J1.GND, R1.Pin_0, R2.Pin_0, R3.Pin_0, R4.Pin_0, R5.Pin_0
  N5: IC1.no_name_yet#10, Raspberry_Pi_1.GIPO8
  N6: IC1.no_name_yet#11, Raspberry_Pi_1.GIPO10
  N7: IC1.no_name_yet#12, Raspberry_Pi_1.GIPO9
  N8: IC1.no_name_yet#13, Raspberry_Pi_1.GIPO11
  3V3: IC1.no_name_yet#15, IC1.no_name_yet#16, Raspberry_Pi_1.3v3, Raspberry_Pi_1.3V3, JP1.SHELL, JP2.SHELL, JP3.SHELL, JP4.SHELL
  N9: Raspberry_Pi_1.GIPO19, Q1.gate, R5.Pin_1
  N10: Q1.drain, J2.GND, D1.anode
  N11: J1.PWR, J2.PWR, D1.cathode

notes:
  12V Power In
  Fan Power Out
  Sensor Inputs
