# Fritzing sketch bbqpi_bonnet (saved by Fritzing 0.9.3b)
breadboards: 1

parts:
  IC1 = MCP3008 8-channel 10-bit ADC [part_number=MCP3008]

nets:
  N1: IC1.no_name_yet#9, IC1.no_name_yet#14
  N2: IC1.no_name_yet#15, IC1.no_name_yet#16
