# Fritzing sketch bbqpi_hat (saved by Fritzing 0.9.3b)

parts:
  Part1 = Adafruit Perma-Proto HAT [part_number="Adafruit #2314 and #2310"]
  IC1 = MCP3008 8-channel 10-bit ADC [part_number=MCP3008]
  JP1 = RCA [package=rca_lock]
  R1 = Resistor [tolerance=±5% resistance=10k package=THT]
  JP2 = RCA [package=rca_lock]
  JP3 = RCA [package=rca_lock]
  JP4 = RCA [package=rca_lock]
  R2 = Resistor [tolerance=±5% resistance=10k package=THT]
  R3 = Resistor [tolerance=±5% resistance=10k package=THT]
  R4 = Resistor [tolerance=±5% resistance=10k package=THT]

nets:
  N1: Part1.SPI_MOSI, Part1.N$49#311
  N2: Part1.SPI_MISO, Part1.N$51#321
  N3: Part1.SPI_SCLK, Part1.N$52#326
  N4: Part1.SPI_CE0, Part1.N$50#316
  N5: Part1.GND, Part1.N$48#306, Part1.N$54#336, R1.Pin_1, R2.Pin_1, R3.Pin_1, R4.Pin_1
  N6: Part1.3.3V, Part1.N$1#160, Part1.N$23#264, Part1.N$53#331
  N7: Part1.N$1#156, JP2.SHELL
  N8: Part1.N$1#157, JP1.SHELL
  N9: Part1.N$7#188, R1.Pin_0
  N10: Part1.N$7#189, JP1.PIN
  N11: Part1.N$7#190, IC1.no_name_yet#1
  N12: Part1.N$9#198, R2.Pin_0
  N13: Part1.N$9#199, JP2.PIN
  N14: Part1.N$9#200, IC1.no_name_yet#2
  N15: Part1.N$10#203, R3.Pin_0
  N16: Part1.N$10#204, JP3.PIN
  N17: Part1.N$10#205, IC1.no_name_yet#3
  N18: Part1.N$11#208, R4.Pin_0
  N19: Part1.N$11#209, JP4.PIN
  N20: Part1.N$11#210, IC1.no_name_yet#4
  N21: Part1.N$12, IC1.no_name_yet#5
  N22: Part1.N$13, IC1.no_name_yet#6
  N23: Part1.N$14, IC1.no_name_yet#7
  N24: Part1.N$15, IC1.no_name_yet#8
  N25: Part1.N$23#261, JP4.SHELL
  N26: Part1.N$23#262, JP3.SHELL
  N27: Part1.N$48#310, IC1.no_name_yet#9
  N28: Part1.N$49#315, IC1.no_name_yet#11
  N29: Part1.N$50#320, IC1.no_name_yet#10
  N30: Part1.N$51#325, IC1.no_name_yet#12
  N31: Part1.N$52#330, IC1.no_name_yet#13
  N32: Part1.N$53#334, Part1.N$55#345
  N33: Part1.N$53#335, IC1.no_name_yet#15
  N34: Part1.N$54#340, IC1.no_name_yet#14
  N35: Part1.N$55#344, IC1.no_name_yet#16

custom parts:
  Adafruit Perma-Proto HAT: To kick off the Adafruit HAT party, we have this Perma-Proto inspired plug in daughter board. It has a grid of 0.1" prototyping soldering holes for attaching chips, resistors, LED, potentiometers and more. The holes are connected underneath with traces to mimic the solderless breadboards you're familiar. There's also long power strips for +3V, +5V and Ground connections to the Pi. Near the top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
